# Fritzing sketch Simon (saved by Fritzing 0.7.0b)
breadboards: 1

parts:
  S1 = Pushbutton [package="[THT]"]
  LED2 = LED - 5mm [color="White (6500K)" package="5 mm [THT]"]
  LED3 = LED - 5mm [color="Red (633nm)" package="5 mm [THT]"]
  LED4 = LED - 5mm [color="Green (555nm)" package="5 mm [THT]"]
  S2 = Pushbutton [package="[THT]"]
  S3 = Pushbutton [package="[THT]"]
  R2 = Resistor [tolerance=±5% resistance=100 package=THT]
  R3 = Resistor [tolerance=±5% resistance=100 package=THT]
  R4 = Resistor [tolerance=±5% resistance=100 package=THT]
  R5 = Resistor [tolerance=±5% resistance=100 package=THT]
  R6 = Resistor [tolerance=±5% resistance=100 package=THT]
  R7 = Resistor [tolerance=±5% resistance=100 package=THT]
  R8 = Resistor [tolerance=±5% resistance=100 package=THT]
  R9 = Resistor [tolerance=±5% resistance=100 package=THT]
  J1 = Piezo Speaker
  LED5 = LED - 5mm [color="Blue (430nm)" package="5 mm [THT]"]
  Arduino1 = Arduino
  S4 = Pushbutton [package="[THT]"]

nets:
  N1: S1.Pin_1, S1.Pin_2, R5.Pin_0, Arduino1.D2
  N2: S1.Pin_3, S1.Pin_4, S2.Pin_3, S2.Pin_4, S3.Pin_3, S3.Pin_4, S4.Pin_3, S4.Pin_4
  N3: LED2.cathode, LED3.cathode, LED4.cathode, LED5.cathode, Arduino1.GND
  N4: LED2.anode, R6.Pin_1
  N5: LED3.anode, R7.Pin_1
  N6: LED4.anode, R8.Pin_1
  N7: S2.Pin_1, S2.Pin_2, R4.Pin_0, Arduino1.D3
  N8: S3.Pin_1, S3.Pin_2, R3.Pin_0, Arduino1.D4
  N9: R2.Pin_0, Arduino1.D5, S4.Pin_1, S4.Pin_2
  N10: R2.Pin_1, R3.Pin_1, R4.Pin_1, R5.Pin_1
  N11: R6.Pin_0, Arduino1.D8
  N12: R7.Pin_0, Arduino1.D9
  N13: R8.Pin_0, Arduino1.D10
  N14: R9.Pin_0, Arduino1.D7
  N15: R9.Pin_1, LED5.anode
  N16: J1.pin2, Arduino1.D12
