# Fritzing sketch simon breadboard (saved by Fritzing 0.7.0b)
breadboards: 1

parts:
  Arduino1 = Arduino
  S1 = Pushbutton [package="[THT]"]
  R1 = Resistor [tolerance=±5% resistance=220 package=THT]
  LED6 = LED - 5mm [color="Blue (430nm)" package="5 mm [THT]"]
  R2 = Resistor [tolerance=±5% resistance=220 package=THT]
  R3 = Resistor [tolerance=±5% resistance=220 package=THT]
  LED7 = LED - 5mm [color="White (6500K)" package="5 mm [THT]"]
  S2 = Pushbutton [package="[THT]"]
  R4 = Resistor [tolerance=±5% resistance=220 package=THT]
  R5 = Resistor [tolerance=±5% resistance=220 package=THT]
  LED8 = LED - 5mm [color="Red (635nm)" package="5 mm [THT]"]
  S3 = Pushbutton [package="[THT]"]
  R6 = Resistor [tolerance=±5% resistance=220 package=THT]
  R7 = Resistor [tolerance=±5% resistance=220 package=THT]
  LED9 = LED - 5mm [color="Green (555nm)" package="5 mm [THT]"]
  S4 = Pushbutton [package="[THT]"]
  R8 = Resistor [tolerance=±5% resistance=220 package=THT]
  J1 = Piezo Speaker

nets:
  N1: Arduino1.GND, R1.Pin_1, LED6.cathode, R3.Pin_1, LED7.cathode, R5.Pin_1, LED8.cathode, R7.Pin_1, LED9.cathode, J1.pin1
  N2: Arduino1.D12, J1.pin2
  N3: Arduino1.D10, R8.Pin_0
  N4: Arduino1.D9, R6.Pin_0
  N5: Arduino1.D8, R4.Pin_0
  N6: Arduino1.D7, R2.Pin_0
  N7: Arduino1.D5, R7.Pin_0, S4.Pin_1, S4.Pin_2
  N8: Arduino1.D4, R5.Pin_0, S3.Pin_1, S3.Pin_2
  N9: Arduino1.D3, R3.Pin_0, S2.Pin_1, S2.Pin_2
  N10: Arduino1.D2, S1.Pin_1, S1.Pin_2, R1.Pin_0
  N11: Arduino1.+5V, S1.Pin_3, S1.Pin_4, S2.Pin_3, S2.Pin_4, S3.Pin_3, S3.Pin_4, S4.Pin_3, S4.Pin_4
  N12: LED6.anode, R2.Pin_1
  N13: LED7.anode, R4.Pin_1
  N14: LED8.anode, R6.Pin_1
  N15: LED9.anode, R8.Pin_1
